# Fritzing sketch uninteruptible (saved by Fritzing 0.8.5b)
breadboards: 1

parts:
  PSU1 = Adjustable Breadboard Power Supply  # not connected
  INA1 = INA219 DC Current Sensor Breakout
  Part1 = Arduino Nano (Rev3.0)
  D1 = Rectifier Diode [part_number=1N4001 package="300 mil [THT]"]
  D2 = Rectifier Diode [part_number=1N4001 package="300 mil [THT]"]
  J1 = Screw terminal - 2 pins [package=THT]
  BATT1 = 4xAA Switchable Battery Pack w/JST connector
  BATT2 = 4xAA Switchable Battery Pack w/JST connector

nets:
  VCC: INA1.VCC, Part1.5V
  GND: INA1.GND, Part1.GND
  N1: INA1.SCL, Part1.A5
  N2: INA1.SDA, Part1.A4
  N3: INA1.Vin-, D1.cathode, J1.pin1
  N4: INA1.Vin+, D2.cathode
  N5: D1.anode, BATT1.POS
  N6: J1.pin2, BATT2.NEG
  N7: BATT1.NEG, BATT2.POS

custom parts:
  INA219 DC Current Sensor Breakout: INA DC Current Sensor Breakout
  4xAA Switchable Battery Pack w/JST connector: 4xAA Switchable Battery Pack with JST connector
